// Logisim project elevator.circ as structural Verilog: 1 circuit, main circuit main
module main (
  input  in_1,
  input  in_2,
  input  in_3,
  input  in_4,
  input  in_5,
  input  in_6
);

  wire and_1_out, and_2_out, and_3_out, and_4_out, and_5_out, and_6_out, and_7_out, and_8_out, and_9_out,
       and_10_out, and_11_out, and_12_out, and_13_out, and_14_out, and_15_out, and_16_out, and_17_out,
       and_18_out, and_19_out, and_20_out, clock_1_out, d_ff_1_q, d_ff_1_qn, d_ff_2_q, d_ff_2_qn, not_1_out,
       not_2_out, not_3_out, not_4_out, not_5_out, not_6_out, or_1_out, or_2_out, or_3_out, or_4_out;
  wire [1:0] not_7_out;
  wire [3:3] not_11_out, not_12_out;
  wire [5:2] not_10_out;

  Clock clock_1 (.out(clock_1_out));
  not not_1 (not_1_out, d_ff_1_q);
  not not_2 (not_2_out, d_ff_2_q);
  not not_3 (not_3_out, in_3);
  not not_4 (not_4_out, in_4);
  not not_5 (not_5_out, in_5);
  not not_6 (not_6_out, in_6);
  and and_1 (and_1_out, not_1_out, not_3_out, not_4_out, not_5_out, in_6);
  or or_1 (or_1_out, and_1_out, and_2_out, and_3_out, and_4_out);
  and and_2 (and_2_out, d_ff_1_q, not_2_out, not_3_out, not_4_out, not_5_out);
  and and_3 (and_3_out, not_2_out, not_3_out, not_5_out, in_6);
  and and_4 (and_4_out, d_ff_1_q, not_2_out, in_6);
  D_Flip_Flop d_ff_1 (.clk(clock_1_out), .D(or_1_out), .Q(d_ff_1_q), .Qn(d_ff_1_qn));  // open: preset, en, reset
  and and_5 (and_5_out, not_1_out, d_ff_2_q, in_4, not_5_out);
  and and_6 (and_6_out, not_1_out, d_ff_2_q, in_4, not_6_out);
  and and_7 (and_7_out, not_1_out, d_ff_2_q, in_3, in_4, in_5, in_6);
  and and_8 (and_8_out, not_1_out, not_2_out, not_3_out, in_5);
  or or_2 (or_2_out, and_5_out, and_6_out, and_7_out, and_8_out, and_10_out, and_9_out, and_11_out, and_12_out, and_13_out);
  and and_9 (and_9_out, not_1_out, d_ff_2_q, not_4_out, in_5);
  and and_10 (and_10_out, d_ff_1_q, not_2_out, in_4, not_6_out);
  and and_11 (and_11_out, not_2_out, not_3_out, in_4, not_6_out);
  D_Flip_Flop d_ff_2 (.clk(clock_1_out), .D(or_2_out), .Q(d_ff_2_q), .Qn(d_ff_2_qn));  // open: preset, en, reset
  and and_12 (and_12_out, not_1_out, d_ff_2_q, not_3_out, not_6_out);
  not not_7 (not_7_out[0], d_ff_2_qn);
  not not_8 (not_7_out[1], d_ff_1_qn);
  and and_13 (and_13_out, d_ff_1_q, not_2_out, in_5, not_6_out);
  Hex_Digit_Display hex_digit_display_1 (.value({{2{in_2}}, not_7_out}));  // open: dp
  or or_3 (or_3_out, and_14_out, and_15_out, and_16_out);
  and and_14 (and_14_out, not_1_out, not_2_out, not_3_out, in_5);
  and and_15 (and_15_out, not_1_out, not_2_out, not_3_out, in_4);
  and and_16 (and_16_out, not_1_out, not_3_out, not_4_out, not_5_out, in_6);
  and and_17 (and_17_out, not_1_out, d_ff_2_q, in_3, not_4_out, not_5_out);
  or or_4 (or_4_out, and_17_out, and_18_out, and_19_out, and_20_out);
  and and_18 (and_18_out, d_ff_1_q, not_2_out, in_3, not_6_out);
  and and_19 (and_19_out, d_ff_1_q, not_2_out, in_4, not_6_out);
  and and_20 (and_20_out, d_ff_1_q, not_2_out, in_5, not_6_out);
  not not_9 (not_10_out[4], or_4_out);
  not not_10 (not_10_out[2], or_3_out);
  nor nor_1 (not_10_out[5], or_4_out, or_3_out);
  not not_11 (not_11_out[3], not_10_out[5]);
  DotMatrix dotmatrix_1 (
    .col0({{3{in_1}}, not_11_out[3], {3{in_1}}}),
    .col1({in_1, not_10_out[5:4], not_10_out[5], not_10_out[2], not_10_out[5], in_1}),
    .col2({in_1, not_10_out[4], {3{not_10_out[5]}}, not_10_out[2], in_1}),
    .col3({in_1, not_10_out[5:4], not_10_out[5], not_10_out[2], not_10_out[5], in_1}),
    .col4({{3{in_1}}, not_12_out[3], {3{in_1}}}));
  not not_12 (not_12_out[3], not_10_out[5]);

  // Notes on the sheet:
  //   GROUND FLOOR UP
  //   FIRST FLOOR DOWN
  //   FIRST FLOOR UP
  //   SECOND FLOOR DOWN
  //   CURRENT FLOOR
  //   ELEVATOR DIRECTION
endmodule
